// Digital circuit mcpu_bram.dig as structural Verilog
module mcpu_bram (
  input  clk
);

  wire add_2_c_o, and_1_out, C_q, d_ff_1_nq, eAk, ePC, i6, i7, sA, wr;
  wire [5:0] add_1_s, blockramdualport_1_d, multiplexer_1_out, multiplexer_3_out, PC_q;
  wire [7:0] add_2_s, Akku_q, multiplexer_2_out, nor_1_out;

  Add #(.Bits(6)) add_1 (.a(multiplexer_3_out), .b({6{1'b0}}), .c_i(1'b1), .s(add_1_s));  // open: c_o
  Add #(.Bits(8)) add_2 (.a(Akku_q), .b({i7, i6, blockramdualport_1_d}), .c_i(1'b0), .s(add_2_s), .c_o(add_2_c_o));
  assign nor_1_out = ~(Akku_q | {i7, i6, blockramdualport_1_d});  // NOr nor_1, 8 bits wide
  Multiplexer #(.Bits(6)) multiplexer_1 (
    .sel(sA), .in_0(add_1_s), .in_1(blockramdualport_1_d), .out(multiplexer_1_out));
  Multiplexer #(.Bits(8)) multiplexer_2 (.sel(i6), .in_0(nor_1_out), .in_1(add_2_s), .out(multiplexer_2_out));
  D_FF d_ff_1 (.D(d_ff_1_nq), .C(clk), .Q(sA), .nQ(d_ff_1_nq));
  Register #(.Bits(6)) PC (.D(multiplexer_1_out), .C(clk), .en(ePC), .Q(PC_q));
  Register #(.Bits(8)) Akku (.D(multiplexer_2_out), .C(clk), .en(eAk), .Q(Akku_q));
  Register C (.D(add_2_c_o), .C(clk), .en(eAk), .Q(C_q));
  Multiplexer #(.Bits(6)) multiplexer_3 (.sel(sA), .in_0(PC_q), .in_1(blockramdualport_1_d), .out(multiplexer_3_out));
  and and_1 (and_1_out, sA, i6, i7, C_q);
  and and_2 (wr, sA, ~i6, i7);  // And
  and and_3 (eAk, sA, ~i7);  // And
  or or_1 (ePC, ~sA, and_1_out);  // Or
  BlockRAMDualPort #(.AddrBits(6), .isProgramMemory("true"), .Bits(8)) blockramdualport_1 (
    .A(multiplexer_3_out), .Din(Akku_q), .str(wr), .C(clk), .D({i7, i6, blockramdualport_1_d}));

  // Other names for the same wires on the sheet: sAk = i6
endmodule
