// Digital circuit system.dig as structural Verilog
module system (
  input  clk,
  input  [14:0] addr,
  input  [15:0] dIn,
  output [15:0] dOut
);

  wire bank_out, rd_out, wr_out;

  ncpu16 ncpu16_1 ();  // open: reset, clock, dIn, address, wr, rd, dOut
  DipSwitch bank (.out(bank_out));
  DipSwitch rd (.out(rd_out));
  DipSwitch wr (.out(wr_out));
  GraphicCard #(.Bits(16)) fb (.A(addr), .str(wr_out), .C(clk), .ld(rd_out), .B(bank_out), .D(dOut));
  assign dOut = wr_out ? dIn : 16'bz;  // Driver driver_1
endmodule
