// Digital circuit av.dig as structural Verilog
// This uses a 4K x 16 bit external memory to generate the timing for a 1280x720 image with
// 80x30 characters, each 16x26 pixels in size. It also generates a new 16 bit audio sample
// on each horizontal line (45 KHz)
module av (
  input  [15:0] dIn,
  input  pclk,
  output [7:0] R,
  output [7:0] G,
  output [7:0] B,
  output H,
  output V,
  output [11:0] X,
  output [11:0] Y,
  output sclk,
  output [15:0] left,
  output [15:0] right,
  output read,
  output [11:0] Addr
);

  wire and_1_out, not_1_out, sub_1_c_o, sub_2_c_o, sub_3_c_o, sub_4_c_o, sub_5_c_o, sub_6_c_o, sub_7_c_o,
       sub_8_c_o, xor_1_out;
  wire [7:0] multiplexer_3_out, multiplexer_4_out, multiplexer_5_out;
  wire [11:0] add_1_s, add_2_s, multiplexer_1_out, multiplexer_2_out;

  Add #(.Bits(12)) add_1 (.a(X), .b({12{1'b0}}), .c_i(1'b1), .s(add_1_s));  // open: c_o
  Add #(.Bits(12)) add_2 (.a(Y), .b({12{1'b0}}), .c_i(1'b1), .s(add_2_s));  // open: c_o
  Multiplexer #(.Bits(12)) multiplexer_1 (.sel(sub_4_c_o), .in_0({12{1'b0}}), .in_1(add_1_s), .out(multiplexer_1_out));
  not not_1 (not_1_out, sub_4_c_o);
  Multiplexer #(.Bits(12)) multiplexer_2 (.sel(sub_8_c_o), .in_0({12{1'b0}}), .in_1(add_2_s), .out(multiplexer_2_out));
  Register #(.Bits(12)) u_x (.D(multiplexer_1_out), .C(pclk), .en(1'b1), .Q(X));
  Register #(.Bits(12)) u_y (.D(multiplexer_2_out), .C(pclk), .en(not_1_out), .Q(Y));
  Sub #(.Bits(12)) sub_1 (.a(X), .b(12'h500), .c_i(1'b0), .c_o(sub_1_c_o));  // open: s
  Sub #(.Bits(12)) sub_2 (.a(X), .b(12'h56e), .c_i(1'b0), .c_o(sub_2_c_o));  // open: s
  Sub #(.Bits(12)) sub_3 (.a(X), .b(12'h596), .c_i(1'b0), .c_o(sub_3_c_o));  // open: s
  Sub #(.Bits(12)) sub_4 (.a(X), .b(12'h671), .c_i(1'b0), .c_o(sub_4_c_o));  // open: s
  Sub #(.Bits(12)) sub_5 (.a(Y), .b(12'h2d0), .c_i(1'b0), .c_o(sub_5_c_o));  // open: s
  Sub #(.Bits(12)) sub_6 (.a(Y), .b(12'h2d5), .c_i(1'b0), .c_o(sub_6_c_o));  // open: s
  Sub #(.Bits(12)) sub_7 (.a(Y), .b(12'h2da), .c_i(1'b0), .c_o(sub_7_c_o));  // open: s
  Sub #(.Bits(12)) sub_8 (.a(Y), .b(12'h2ed), .c_i(1'b0), .c_o(sub_8_c_o));  // open: s
  xor xor_1 (xor_1_out, Y[3], X[3]);
  and and_1 (and_1_out, sub_1_c_o, sub_5_c_o);
  and and_2 (H, ~sub_2_c_o, sub_3_c_o);  // And
  and and_3 (V, ~sub_6_c_o, sub_7_c_o);  // And
  Multiplexer #(.Bits(8)) multiplexer_3 (
    .sel(xor_1_out), .in_0({Y[8:7], Y[8:7], Y[8:7], Y[8:7]}), .in_1({X[9:8], X[9:8], X[9:8], X[9:8]}),
    .out(multiplexer_3_out));
  Multiplexer #(.Bits(8)) multiplexer_4 (
    .sel(xor_1_out), .in_0({Y[6:5], Y[6:5], Y[6:5], Y[6:5]}), .in_1({X[7:6], X[7:6], X[7:6], X[7:6]}),
    .out(multiplexer_4_out));
  Multiplexer #(.Bits(8)) multiplexer_5 (
    .sel(xor_1_out), .in_0({8{Y[4]}}), .in_1({X[5:4], X[5:4], X[5:4], X[5:4]}), .out(multiplexer_5_out));
  Multiplexer #(.Bits(8)) multiplexer_6 (.sel(and_1_out), .in_0({8{1'b0}}), .in_1(multiplexer_3_out), .out(R));
  Multiplexer #(.Bits(8)) multiplexer_7 (.sel(and_1_out), .in_0({8{1'b0}}), .in_1(multiplexer_4_out), .out(G));
  Multiplexer #(.Bits(8)) multiplexer_8 (.sel(and_1_out), .in_0({8{1'b0}}), .in_1(multiplexer_5_out), .out(B));

  assign Addr = {12{1'b0}};
  assign left = {16{1'b0}};
  assign read = 1'b0;
  assign right = {16{1'b0}};
  assign sclk = 1'b0;

  // Other names for the same wires on the sheet: fb[7:0] = {X[5:4], X[5:4], X[5:4], X[5:4]};
  //   fg[7:0] = {X[7:6], X[7:6], X[7:6], X[7:6]}; fr[7:0] = {X[9:8], X[9:8], X[9:8], X[9:8]}; bb[7:0] = {8{Y[4]}};
  //   bg[7:0] = {Y[6:5], Y[6:5], Y[6:5], Y[6:5]}; br[7:0] = {Y[8:7], Y[8:7], Y[8:7], Y[8:7]}

  // Notes on the sheet:
  //   pclk: Hz: 2147483647
  //   60 Hz, 74.25 MHz, 45 KHz, 1280, 110, 40, 220, 720, 5, 5, 20, false, false
endmodule
