// Digital circuit drv16.dig as structural Verilog
// 16 bit processor which is compatible at the assembly language level with RISC-V
module drv16 (
  input  clock,
  input  reset,
  input  [15:0] dIn,
  output [14:0] addr,
  output wr,
  output [15:0] dOut,
  output rd
);

  wire ALU_ge, ALU_ne, controlunit_1_azero, controlunit_1_logic, controlunit_1_selimm, controlunit_1_selrd,
       controlunit_1_sign, controlunit_1_slt, controlunit_1_sub, controlunit_1_we, controlunit_1_word;
  wire [0:0] ALU_r, not_1_out;
  wire [1:0] controlunit_1_logselect;
  wire [3:0] controlunit_1_ra, controlunit_1_rb, controlunit_1_rw;
  wire [15:0] bytes_1_tord, controlunit_1_imm, multiplexer_1_out, multiplexer_2_out, multiplexer_3_out,
       multiplexer_4_out, registerfile_1_da, registerfile_1_db;

  controlUnit controlunit_1 (
    .clock(clock), .reset(reset), .dIn(dIn), .NE(ALU_ne), .GE(ALU_ge), .wr(wr), .rd(rd),
    .sign(controlunit_1_sign), .word(controlunit_1_word), .sub(controlunit_1_sub),
    .\logic (controlunit_1_logic), .logSelect(controlunit_1_logselect), .Imm(controlunit_1_imm),
    .selImm(controlunit_1_selimm), .Azero(controlunit_1_azero), .we(controlunit_1_we), .Rw(controlunit_1_rw),
    .Ra(controlunit_1_ra), .Rb(controlunit_1_rb), .selRd(controlunit_1_selrd), .slt(controlunit_1_slt));
  not not_1 (not_1_out[0], ALU_ge);
  Multiplexer #(.Bits(16)) multiplexer_1 (
    .sel(controlunit_1_slt), .in_0({addr, ALU_r[0]}), .in_1({{15{1'b0}}, not_1_out[0]}),
    .out(multiplexer_1_out));
  // Probe rS2 on controlunit_1_rb
  // Probe rS1 on controlunit_1_ra
  // Probe rD on controlunit_1_rw
  Multiplexer #(.Bits(16)) multiplexer_2 (
    .sel(controlunit_1_selrd), .in_0(multiplexer_1_out), .in_1(bytes_1_tord), .out(multiplexer_2_out));
  // Probe selImm on controlunit_1_selimm
  // Probe we on controlunit_1_we
  RegisterFile #(.AddrBits(4), .Bits(16)) registerfile_1 (
    .Din(multiplexer_2_out), .we(controlunit_1_we), .Rw(controlunit_1_rw), .C(clock), .Ra(controlunit_1_ra),
    .Rb(controlunit_1_rb), .Da(registerfile_1_da), .Db(registerfile_1_db));
  // Probe dA on registerfile_1_da
  // Probe dB on registerfile_1_db
  bytes bytes_1 (
    .dIn(dIn), .sign(controlunit_1_sign), .word(controlunit_1_word), .A0(ALU_r[0]),
    .fromRS2(registerfile_1_db), .dOut(dOut), .toRD(bytes_1_tord));
  Multiplexer #(.Bits(16)) multiplexer_3 (
    .sel(controlunit_1_azero), .in_0(registerfile_1_da), .in_1({16{1'b0}}), .out(multiplexer_3_out));
  Multiplexer #(.Bits(16)) multiplexer_4 (
    .sel(controlunit_1_selimm), .in_0(registerfile_1_db), .in_1(controlunit_1_imm), .out(multiplexer_4_out));
  // Probe A on multiplexer_3_out
  alu ALU (
    .R({addr, ALU_r[0]}), .A(multiplexer_3_out), .B(multiplexer_4_out), .sub(controlunit_1_sub),
    .logSelect(controlunit_1_logselect), .\logic (controlunit_1_logic), .NE(ALU_ne), .GE(ALU_ge));
  // Probe B on multiplexer_4_out
  // Probe NE on ALU_ne
  // Probe GE on ALU_ge

  // Notes on the sheet:
  //   addr: selects a 16 bit word in memory to be read or changed
  //   wr: indicates a write operation
  //   dOut: word to be sent to memory
  //   reset: when high prepares the processor to execute from address 0
  //   dIn: word coming from memory
  //   rd: indicates that memory will be read in this cycle
endmodule
