// Digital circuit system.dig as structural Verilog
// A simple system with a drv16 processor, 64KB of RAM, a terminal and keyboard
module system (
  input  clk,
  output [31:0] cnt
);

  wire cpu_rd, cpu_wrh, cpu_wrl, reset_out;
  wire [14:0] cpu_addr;
  wire [15:0] cpu_dout, mem0_low_d, termcnt_1_dout;

  DipSwitch reset (.out(reset_out));
  // Probe dIn on termcnt_1_dout
  drv16 cpu (
    .clock(clk), .reset(reset_out), .dIn(termcnt_1_dout), .addr(cpu_addr), .dOut(cpu_dout), .rd(cpu_rd),
    .wrH(cpu_wrh), .wrL(cpu_wrl));
  // Probe addr on cpu_addr
  RAMDualPort #(.AddrBits(15), .isProgramMemory("true"), .Bits(8)) mem0_low (
    .A(cpu_addr), .Din(cpu_dout[7:0]), .str(cpu_wrl), .C(clk), .ld(cpu_rd), .D(mem0_low_d[7:0]));
  RAMDualPort #(.AddrBits(15), .isProgramMemory("true"), .Bits(8)) mem1_high (
    .A(cpu_addr), .Din(cpu_dout[15:8]), .str(cpu_wrh), .C(clk), .ld(cpu_rd), .D(mem0_low_d[15:8]));
  termcnt termcnt_1 (
    .relogio(clk), .write(cpu_wrl), .read(cpu_rd), .Addr({{17{1'b1}}, cpu_addr}), .dMemOut(mem0_low_d),
    .dIn(cpu_dout), .dOut(termcnt_1_dout), .cnt(cnt));

  // Notes on the sheet:
  //   clk: Hz: 2147483647
  //   cnt: number of clocks for benchmark
endmodule
